# Fritzing sketch Gate (saved by Fritzing 0.9.3b)

parts:
  OLED_I2C1 = OLED 128x64 I2C Monochrome Display
  E1 = ESP32-Cam
  M1 = fc-51 [package=THT]

nets:
  N1: OLED_I2C1.SDA, E1.GPIO_15
  N2: OLED_I2C1.SCK, E1.GPIO_14
  VDD: OLED_I2C1.VDD, E1.5V, M1.pin3
  GND: OLED_I2C1.GND, E1.GND, M1.pin2
  N3: E1.GPIO_13, M1.pin1
