# Fritzing sketch Node (saved by Fritzing 0.9.3b)

parts:
  E1 = ESP32-Cam
  M1 = fc-51 [package=THT]
  U1 = WS2812 RGB LED strip

nets:
  5V: E1.5V, M1.pin3, U1.VCC
  GND: E1.GND, M1.pin2, U1.GND
  N1: E1.GPIO_12, U1.DOUT
  N2: E1.GPIO_13, M1.pin1

custom parts:
  WS2812 RGB LED strip: WS2812 strip
